// Logisim project Lab_1.circ as structural Verilog: 11 circuits, main circuit main
module main (
  input  in_1,
  output [3:0] out_2,
  output [7:0] out_3,
  output [7:0] out_4,
  output [7:0] AB,
  output [7:0] BB
);

  wire CLK1_out, clock_1_out, clock_2_out, comparador_8bits_1_out_3, dipswitch_1_sw1, not_2_out;
  wire [4:0] multiplexer_1_out;
  wire [4:4] not_1_out;

  Clock #(.highDuration(2)) clock_1 (.out(clock_1_out));
  not not_1 (not_1_out[4], 1'b1);
  Clock clock_2 (.out(clock_2_out));
  Contador_4BITS contador_4bits_1 (.CLK(clock_1_out), .RUN(in_1), .out_3(out_2));
  RAM #(.addrWidth(5)) ram_1 (
    .addr(multiplexer_1_out), .oe(1'b1), .clk(clock_2_out), .din(out_4), .dout(out_3));  // open: we
  Multiplexer #(.width(5)) multiplexer_1 (
    .in0({not_1_out[4], out_2}), .in1({1'b1, out_2}), .out(multiplexer_1_out), .sel(clock_1_out));
  DipSwitch #(.number(2)) dipswitch_1 (.sw1(dipswitch_1_sw1));  // open: sw2
  not not_2 (not_2_out, CLK1_out);
  Clock #(.highDuration(2), .lowDuration(2)) CLK1 (.out(CLK1_out));
  flipflopDx8 flipflopdx8_1 (.opn(out_3), .CLK(CLK1_out), .R(dipswitch_1_sw1), .ext(AB));  // open: extn
  flipflopDx8 flipflopdx8_2 (.opn(out_3), .CLK(not_2_out), .R(dipswitch_1_sw1), .ext(BB));  // open: extn
  Multiplexer #(.width(8)) multiplexer_2 (.in0(AB), .in1(BB), .out(out_4), .sel(comparador_8bits_1_out_3));
  comparador_8bits comparador_8bits_1 (.A(AB), .B(BB), .out_3(comparador_8bits_1_out_3));  // open: out_4, out_5

  // Notes on the sheet:
  //   DATA
  //   B
endmodule

module flip_flop_JK (
  input  J,
  input  CLK,
  input  K
);

  wire nand_1_out, nand_2_out, nand_3_out, nand_4_out;

  nand nand_1 (nand_1_out, nand_4_out, J, CLK);
  nand nand_2 (nand_2_out, CLK, K, nand_3_out);
  nand nand_3 (nand_3_out, nand_1_out, nand_4_out);
  nand nand_4 (nand_4_out, nand_3_out, nand_2_out);
  LED led_1 (.in(nand_3_out));
  LED led_2 (.in(nand_4_out));
endmodule

module comparador_menor (
  input  [7:0] A,
  input  [7:0] B
);
endmodule

module comparador_2bits (
  input  [1:0] A,
  input  [1:0] B,
  output AmyB,
  output AigB,
  output AmnB
);

  wire and_1_out, and_2_out, and_3_out, and_4_out, and_5_out, and_6_out, and_7_out, and_8_out, and_9_out,
       and_10_out, not_1_out, not_2_out, not_3_out, not_4_out;

  not not_1 (not_1_out, A[1]);
  not not_2 (not_2_out, A[0]);
  not not_3 (not_3_out, B[1]);
  not not_4 (not_4_out, B[0]);
  and and_1 (and_1_out, A[1], not_3_out);
  and and_2 (and_2_out, A[1], A[0], not_4_out);
  and and_3 (and_3_out, A[0], not_3_out, not_4_out);
  and and_4 (and_4_out, not_1_out, not_2_out, not_3_out, not_4_out);
  and and_5 (and_5_out, not_1_out, A[0], not_3_out, B[0]);
  and and_6 (and_6_out, A[1], A[0], B[1], B[0]);
  and and_7 (and_7_out, A[1], not_2_out, B[1], not_4_out);
  and and_8 (and_8_out, not_1_out, B[1]);
  and and_9 (and_9_out, not_1_out, not_2_out, B[0]);
  and and_10 (and_10_out, not_1_out, not_2_out, B[0]);
  or or_1 (AmyB, and_1_out, and_2_out, and_3_out);
  or or_2 (AigB, and_4_out, and_5_out, and_6_out, and_7_out);
  or or_3 (AmnB, and_8_out, and_9_out, and_10_out);
endmodule

module comparador_4bits (
  input  [3:0] A,
  input  [3:0] B,
  output out_3,
  output out_4,
  output out_5
);

  wire [2:0] comparador_2bits_1_amyb, comparador_2bits_2_amyb;

  comparador_2bits comparador_2bits_1 (
    .A(A[3:2]), .B(B[3:2]), .AmyB(comparador_2bits_1_amyb[0]), .AigB(comparador_2bits_1_amyb[1]),
    .AmnB(comparador_2bits_1_amyb[2]));
  comparador_2bits comparador_2bits_2 (
    .A(A[1:0]), .B(B[1:0]), .AmyB(comparador_2bits_2_amyb[0]), .AigB(comparador_2bits_2_amyb[1]),
    .AmnB(comparador_2bits_2_amyb[2]));
  comparador comparador_1 (
    .MasS(comparador_2bits_1_amyb), .MenosS(comparador_2bits_2_amyb), .mayor(out_3), .igual(out_4),
    .menor(out_5));
endmodule

module comparador_8bits (
  input  [7:0] A,
  input  [7:0] B,
  output out_3,
  output out_4,
  output out_5
);

  wire [2:0] comparador_4bits_1_out_3, comparador_4bits_2_out_3;

  comparador_4bits comparador_4bits_1 (
    .A(A[7:4]), .B(B[7:4]), .out_3(comparador_4bits_1_out_3[0]), .out_4(comparador_4bits_1_out_3[1]),
    .out_5(comparador_4bits_1_out_3[2]));
  comparador_4bits comparador_4bits_2 (
    .A(A[3:0]), .B(B[3:0]), .out_3(comparador_4bits_2_out_3[0]), .out_4(comparador_4bits_2_out_3[1]),
    .out_5(comparador_4bits_2_out_3[2]));
  comparador comparador_1 (
    .MasS(comparador_4bits_1_out_3), .MenosS(comparador_4bits_2_out_3), .mayor(out_3), .igual(out_4),
    .menor(out_5));
endmodule

module comparador (
  input  [2:0] MasS,
  input  [2:0] MenosS,
  output mayor,
  output igual,
  output menor
);

  wire and_1_out, and_2_out;

  and and_1 (and_1_out, MasS[1], MenosS[0]);
  and and_2 (and_2_out, MasS[1], MenosS[2]);
  or or_1 (mayor, MasS[0], and_1_out);
  and and_3 (igual, MasS[1], MenosS[1]);
  or or_2 (menor, and_2_out, MasS[2]);
endmodule

module decodificador (
  input  [2:0] in_1,
  input  [1:0] in_2,
  input  [1:0] in_3,
  input  [1:0] in_4,
  input  [1:0] in_5,
  input  [1:0] in_6,
  input  [1:0] in_7,
  input  [1:0] in_8,
  input  [1:0] in_9,
  input  [2:0] in_10,
  input  [1:0] in_11,
  input  [2:0] in_12,
  output [7:0] out_13,
  output [7:0] out_14,
  output [1:0] out_15,
  output [1:0] out_16,
  output [1:0] out_17,
  output [1:0] out_18,
  output [1:0] out_19,
  output [1:0] out_20,
  output [1:0] out_21,
  output [1:0] out_22,
  output [1:0] out_23
);

  wire clock_1_out, dipswitch_1_sw1;

  Clock clock_1 (.out(clock_1_out));
  Decoder #(.select(3)) decoder_1 (
    .out0(out_14[0]), .out1(out_14[1]), .out2(out_14[2]), .out3(out_14[3]), .out4(out_14[4]),
    .out5(out_14[5]), .out6(out_14[6]), .out7(out_14[7]), .sel(in_1), .en(clock_1_out));
  Demultiplexer #(.select(3), .width(2)) demultiplexer_1 (
    .out0(out_16), .out1(out_17), .out2(out_18), .out3(out_19), .out4(out_20), .out5(out_21), .out6(out_22),
    .out7(out_23), .in(in_11), .sel(in_12));
  Multiplexer #(.select(3), .width(2)) multiplexer_1 (
    .in0(in_2), .in1(in_3), .in2(in_4), .in3(in_5), .in4(in_6), .in5(in_7), .in6(in_8), .in7(in_9),
    .out(out_15), .sel(in_10));
  DipSwitch #(.number(2)) dipswitch_1 (.sw1(dipswitch_1_sw1));  // open: sw2
  Demultiplexer #(.select(3), .width(8)) demultiplexer_2 (.in(out_13));  // open: out0, out1, out2, out3, out4, out5, out6, out7, sel
  flipflopDx8 flipflopdx8_1 (.opn(out_14), .CLK(clock_1_out), .R(dipswitch_1_sw1), .ext(out_13));  // open: extn
  _7_Segment_Display #(.active("false")) u_7_segment_display_1 ();  // open: g, f, a, b, e, d, c, dp
endmodule

module flipflopDx8 (
  input  [7:0] opn,
  input  CLK,
  input  R,
  output [7:0] ext,
  output [7:0] extn
);

  wire undriven;

  D_Flip_Flop d_ff_1 (.D(opn[0]), .clk(CLK), .Q(ext[0]), .Qn(extn[0]), .reset(undriven));  // open: preset
  D_Flip_Flop d_ff_2 (.D(opn[1]), .clk(CLK), .Q(ext[1]), .Qn(extn[1]), .reset(undriven));  // open: preset
  D_Flip_Flop d_ff_3 (.D(opn[2]), .clk(CLK), .Q(ext[2]), .Qn(extn[2]), .reset(undriven));  // open: preset
  D_Flip_Flop d_ff_4 (.D(opn[3]), .clk(CLK), .Q(ext[3]), .Qn(extn[3]), .reset(undriven));  // open: preset
  D_Flip_Flop d_ff_5 (.D(opn[4]), .clk(CLK), .Q(ext[4]), .Qn(extn[4]), .reset(undriven));  // open: preset
  D_Flip_Flop d_ff_6 (.D(opn[5]), .clk(CLK), .Q(ext[5]), .Qn(extn[5]), .reset(undriven));  // open: preset
  D_Flip_Flop d_ff_7 (.D(opn[6]), .clk(CLK), .Q(ext[6]), .Qn(extn[6]), .reset(undriven));  // open: preset
  D_Flip_Flop d_ff_8 (.D(opn[7]), .clk(CLK), .Q(ext[7]), .Qn(extn[7]), .reset(undriven));  // open: preset
endmodule

module maquina_estados_JK (
);

  Contador_4BITS contador_4bits_1 ();  // open: CLK, RUN, out_3
endmodule

module Contador_4BITS (
  input  CLK,
  input  RUN,
  output [3:0] out_3
);

  wire and_1_out, and_2_out, and_3_out;

  and and_1 (and_1_out, CLK, RUN);
  and and_2 (and_2_out, out_3[1], out_3[0], out_3[2]);
  and and_3 (and_3_out, out_3[1], out_3[0]);
  J_K_Flip_Flop A (.J(and_2_out), .K(and_2_out), .clk(and_1_out), .Q(out_3[3]));  // open: Qn, preset, reset
  J_K_Flip_Flop B (.J(and_3_out), .K(and_3_out), .clk(and_1_out), .Q(out_3[2]));  // open: Qn, preset, reset
  J_K_Flip_Flop C (.J(out_3[0]), .K(out_3[0]), .clk(and_1_out), .Q(out_3[1]));  // open: Qn, preset, reset
  J_K_Flip_Flop D (.J(1'b1), .K(1'b1), .clk(and_1_out), .Q(out_3[0]));  // open: Qn, preset, reset
endmodule
